# Fritzing sketch Wiring (saved by Fritzing 0.9.3b)
breadboards: 1

parts:
  DFPlayer_Mini1 = DFPlayer MINI [package="DIP (Dual Inline) [THT]"]
  SPKR1 = Loudspeaker
  R1 = Resistor [tolerance=±5% resistance=1k package=THT]
  R2 = Resistor [tolerance=±5% resistance=1k package=THT]
  Composant2 = Real Time Clock Module - DS1307 RTC Breakout Board
  Composant3 = Arduino Uno (Rev3)
  X1 = USB Connectors [package=usb-a-s-nosilk-female]
  R3 = Rotary Potentiometer (Small) [maximum_resistance=100kΩ package=THT]
  JP3 = Header 4 [package=screwterminal-3.5mm-4_lock]
  JP2 = Header 4 [package=screwterminal-3.5mm-4_lock]
  SPKR2 = Loudspeaker  # not connected
  SPKR3 = Loudspeaker  # not connected
  S1 = SWITCH-MOMENTARY-2 [package=tactile-pth-12mm]  # not connected
  S2 = SWITCH-MOMENTARY-2 [package=tactile-pth-12mm]  # not connected

nets:
  VCC: DFPlayer_Mini1.VCC, Composant3.5V, X1.D+, R3.leg2, JP2.1
  N1: DFPlayer_Mini1.RX, R1.Pin_1
  N2: DFPlayer_Mini1.TX, R2.Pin_1
  N3: DFPlayer_Mini1.SPK1, SPKR1.pin2
  GND: DFPlayer_Mini1.GND, Composant3.GND, X1.D-, R3.leg1, JP2.2
  N4: DFPlayer_Mini1.SPK2, SPKR1.pin1
  N5: R1.Pin_0, Composant3.D0/RX
  N6: R2.Pin_0, Composant3.D1/TX
  N7: Composant2.SCL, Composant3.A5/SCL
  N8: Composant2.SDA, Composant3.A4/SDA
  N9: Composant3.D8, JP2.4
  N10: Composant3.D9_PWM, JP3.1
  N11: Composant3.D10_PWM/SS, JP2.3
  N12: Composant3.D11_PWM/MOSI, JP3.2
  N13: Composant3.D13/SCK, JP3.3
  N14: Composant3.D3_PWM, R3.wiper
  N15: Composant3.3V3, JP3.4

notes:
  3W, 5V = 0.6A
  1k Ohm
  speakers(0.1A) + arduino + TFT
  VCC - GND - CS - RESET - A0 - SDA - SCK - LED
  10W, 5V = 2A
  0.5W, 5V = 0.1A
  LESS THAN 3W !!!
  Button Validate
  Button Choice
  Potentiometer choice

custom parts:
  DFPlayer MINI: MP3 module by DFRobot.com for playing Music from an SD-Card. Supports WAV and MP3 files.
